// Logisim project ex3.circ as structural Verilog: 1 circuit, main circuit AddMachine
module AddMachine (
  input  clk,
  output [7:0] ADD_OUT,
  output [7:0] REG_OUT
);

  wire clock_1_out;

  Clock clock_1 (.out(clock_1_out));
  Adder adder_1 (.a(8'h1), .b(REG_OUT), .out(ADD_OUT));  // open: cin, cout
  Register register_1 (.D(ADD_OUT), .en(clock_1_out), .clk(clock_1_out), .Q(REG_OUT));  // open: clr
endmodule
