// Logisim project ex7.circ as structural Verilog: 5 circuits, main circuit FSM
module FSM (
  input  clk,
  output [1:0] OUTPUT0
);

  wire clock_1_out, helper_1_out_green, helper_1_out_red, helper_1_out_yellow, Input0;
  wire [1:0] fsmlogic_1_next_state, register_1_q;

  FSMLogic fsmlogic_1 (
    .INPUT0(Input0), .CURRENT_STATE(register_1_q), .OUTPUT0(OUTPUT0), .NEXT_STATE(fsmlogic_1_next_state));
  Clock clock_1 (.out(clock_1_out));
  Register #(.width(2)) register_1 (.D(fsmlogic_1_next_state), .clk(clock_1_out), .Q(register_1_q));  // open: en, clr
  Helper helper_1 (
    .IN0(OUTPUT0[0]), .IN1(OUTPUT0[1]), .CLOCK0(clk), .TRIGGER_SIG(Input0), .OUT_RED(helper_1_out_red),
    .OUT_YELLOW(helper_1_out_yellow), .OUT_GREEN(helper_1_out_green));
  LED RED (.in(helper_1_out_red));
  LED YELLOW (.in(helper_1_out_yellow));
  LED GREEN (.in(helper_1_out_green));

  // Other names for the same wires on the sheet: CLOCK0 = clk; OUT0 = OUTPUT0[0]; OUT1 = OUTPUT0[1]
endmodule

module StateBit1 (
  input  INPUT0,
  input  [1:0] CURRENT_STATE,
  output NEW_STATE_BIT_1
);

  wire and_1_out, and_2_out, and_3_out, not_1_out, not_2_out, not_3_out;

  not not_1 (not_1_out, INPUT0);
  not not_2 (not_2_out, CURRENT_STATE[0]);
  not not_3 (not_3_out, CURRENT_STATE[1]);
  and and_1 (and_1_out, CURRENT_STATE[0], not_3_out);
  and and_2 (and_2_out, not_1_out, CURRENT_STATE[1]);
  and and_3 (and_3_out, INPUT0, and_1_out);
  or or_1 (NEW_STATE_BIT_1, and_2_out, and_3_out);
endmodule

module StateBit0 (
  input  INPUT0,
  input  [1:0] CURRENT_STATE,
  output NEW_STATE_BIT_0
);

  wire and_1_out, and_2_out, and_3_out, not_1_out, not_2_out, not_3_out;

  not not_1 (not_1_out, INPUT0);
  not not_2 (not_2_out, CURRENT_STATE[0]);
  not not_3 (not_3_out, CURRENT_STATE[1]);
  and and_1 (and_1_out, not_2_out, not_3_out);
  and and_2 (and_2_out, not_1_out, CURRENT_STATE[0]);
  and and_3 (and_3_out, INPUT0, and_1_out);
  or or_1 (NEW_STATE_BIT_0, and_2_out, and_3_out);
endmodule

module FSMLogic (
  input  INPUT0,
  input  [1:0] CURRENT_STATE,
  output [1:0] OUTPUT0,
  output [1:0] NEXT_STATE
);

  StateBit0 statebit0_1 (.INPUT0(INPUT0), .CURRENT_STATE(CURRENT_STATE), .NEW_STATE_BIT_0(NEXT_STATE[0]));
  StateBit1 statebit1_1 (.INPUT0(INPUT0), .CURRENT_STATE(CURRENT_STATE), .NEW_STATE_BIT_1(NEXT_STATE[1]));

  assign OUTPUT0 = NEXT_STATE;

  // Other names for the same wires on the sheet: CurrentState[1:0] = CURRENT_STATE
endmodule

module Helper (
  input  IN0,
  input  IN1,
  input  CLOCK0,
  output TRIGGER_SIG,
  output OUT_RED,
  output OUT_YELLOW,
  output OUT_GREEN
);

  not not_1 (TRIGGER_SIG, CLOCK0);
  nor nor_1 (OUT_RED, IN1, IN0);
  and and_1 (OUT_YELLOW, IN1, ~IN0);  // AND_Gate
  and and_2 (OUT_GREEN, ~IN1, IN0);  // AND_Gate
endmodule
